// Digital circuit alu1.dig as structural Verilog
module alu1 (
  input  Op1,
  input  Op0,
  input  A_i,
  input  B_i,
  input  compl_1,
  input  ci_1,
  output S_i,
  output ci
);

  wire and_1_out, mux2_1_p3, mux4_1_p3, mux4_1_p4, mux4_1_p5, sum1_1_p4;

  and and_1 (and_1_out, A_i, B_i);
  // mux4 mux4_1: pin names not known; wires that end beside it: and_1_out, S_i, mux4_1_p3, mux4_1_p4, mux4_1_p5, Op1, Op0
  or or_1 (mux4_1_p3, A_i, B_i);
  xor xor_1 (mux4_1_p4, A_i, B_i);
  // sum1 sum1_1: pin names not known; wires that end beside it: ci, mux4_1_p5, A_i, sum1_1_p4, ci_1
  // mux2 mux2_1: pin names not known; wires that end beside it: B_i, sum1_1_p4, mux2_1_p3, compl_1
  not not_1 (mux2_1_p3, B_i);

  // Notes on the sheet:
  //   Op1: Operation select, line 1
  //   {{es Linea 1 de seleccion de operacion}}
  //   Op0: Operation select, line 0
  //   {{es Linea 0 de seleccion de operacion}}
  //   A_i: Bit i of operand A
  //   {{es Bit i del operando A}}
  //   B_i: Bit i of operand B
  //   {{es Bit i del operando B}}
  //   compl_1: One's complement input
  //   {{es Linea de complemento a 1}}
  //   ci_1: Previous carry input
  //   {{es Acarreo de entrada}}
  //   S_i: Bit i of the result
  //   {{es Bit i del resultado}}
  //   ci: Carry output
  //   {{es Acarreo de salida}}
endmodule
