// Digital circuit gen_ov_s.dig as structural Verilog
module gen_ov_s (
  input  A_n_1,
  input  B_n_1,
  input  S_n_1,
  output Ov
);

  wire and_1_out, and_2_out;

  and and_1 (and_1_out, ~A_n_1, ~B_n_1, S_n_1);  // And
  and and_2 (and_2_out, A_n_1, B_n_1, ~S_n_1);  // And
  or or_1 (Ov, and_1_out, and_2_out);

  // Notes on the sheet:
  //   Ov: Overflow output
  //   {{es Salida de overflow}}
  //   A_n_1: Sign bit of the first summand
  //   {{es Bit de signo del primer sumando}}
  //   B_n_1: Sign bit of the second summand
  //   {{es Bit de signo del segundo sumando}}
  //   S_n_1: Sign bit of the addition
  //   {{es Bit de signo de la suma}}
endmodule
