// Digital circuit sum1.dig as structural Verilog
module sum1 (
  input  A_i,
  input  B_i,
  input  c_i_1,
  output c_i,
  output S_i
);

  wire and_1_out, and_2_out, xor_2_out;

  or or_1 (c_i, and_2_out, and_1_out);
  and and_1 (and_1_out, c_i_1, xor_2_out);
  xor xor_1 (S_i, xor_2_out, c_i_1);
  xor xor_2 (xor_2_out, A_i, B_i);
  and and_2 (and_2_out, A_i, B_i);

  // Notes on the sheet:
  //   A_i: Bit i of operand A
  //   {{es Bit i del operando A}}
  //   B_i: Bit i of operand B
  //   {{es Bit i del operando B}}
  //   c_i_1: Previous carry input
  //   {{es Acarreo de entrada}}
  //   c_i: Carry output
  //   {{es Acarreo de salida}}
  //   S_i: Bit i of the result
  //   {{es Bit i del resultado}}
endmodule
