// Digital circuit overflow.dig as structural Verilog
// Detector de overflow para la suma
module overflow (
  input  A_n_1,
  input  B_n_1,
  input  S_n_1,
  output Ov
);

  wire and_1_out, and_2_out;

  and and_1 (and_1_out, ~A_n_1, ~B_n_1, S_n_1);  // And
  and and_2 (and_2_out, A_n_1, B_n_1, ~S_n_1);  // And
  or or_1 (Ov, and_1_out, and_2_out);

  // Notes on the sheet:
  //   Detector de overflow para la suma
endmodule

/* Test case:
A_{n-1} B_{n-1} S_{n-1} Ov
0        0      0       0
0        0      1       1
0        1      0       0
0        1      1       0
1        0      0       0
1        0      1       0
1        1      0       1
1        1      1       0
*/
