// Digital circuit p.dig as structural Verilog
module p (
  input  A_n_1,
  input  B_n_1,
  output S_n_1
);

  xor xor_1 (S_n_1, A_n_1, B_n_1);

  // Notes on the sheet:
  //   A_n_1: Primera entrada
  //   B_n_1: Segunda entrada
  //   S_n_1: Salida de overflow
endmodule
